// Logisim project battleship.circ as structural Verilog: 3 circuits, main circuit main
module main (
  input  [3:0] in_1,
  input  in_2,
  output out_3,
  output out_4,
  output out_5,
  output out_6,
  output out_7,
  output out_8,
  output out_9,
  output out_10
);

  // Encoder encoder_1: pin names not known; wires that end beside it: in_1, out_4, out_6
endmodule

module decodificador (
  input  A,
  input  B,
  output out_3,
  output out_4,
  output out_5,
  output out_6
);

  and and_1 (out_3, A, B);
  and and_2 (out_4, ~B, A);  // AND_Gate
  and and_3 (out_5, B, ~A);  // AND_Gate
  and and_4 (out_6, ~B, ~A);  // AND_Gate
endmodule

module Encoder (
  input  [3:0] Navio,
  output [3:0] x
);

  wire and_3_out, and_4_out, and_5_out, and_6_out, and_7_out, and_8_out, not_1_out, not_2_out, not_3_out,
       not_4_out;

  not not_1 (not_1_out, Navio[3]);
  not not_2 (not_2_out, Navio[2]);
  not not_3 (not_3_out, Navio[1]);
  not not_4 (not_4_out, Navio[0]);
  and and_1 (x[3], Navio[3], Navio[2], not_3_out, not_4_out);
  and and_2 (x[2], Navio[3], Navio[1], Navio[0]);
  and and_3 (and_3_out, not_1_out, not_2_out, not_4_out);
  and and_4 (and_4_out, not_1_out, Navio[2], Navio[0]);
  and and_5 (and_5_out, not_1_out, not_2_out, Navio[0]);
  and and_6 (and_6_out, not_1_out, Navio[2], not_4_out);
  and and_7 (and_7_out, Navio[3], not_3_out, Navio[0]);
  and and_8 (and_8_out, Navio[3], Navio[1], not_4_out);
  or or_1 (x[1], and_3_out, and_4_out);
  or or_2 (x[0], and_5_out, and_6_out, and_7_out, and_8_out);
endmodule
